# Fritzing sketch Balance_Robot_Wiring (saved by Fritzing 0.9.4)

parts:
  Main_Arduino = Arduino Uno (Rev3)
  Motor_Controller_Arduino = Arduino Nano (Rev3.0)
  Pololu_A1 = Pololu A4988 [package=SO16]
  Pololu_A2 = Pololu A4988 [package=SO16]
  M1 = Stepper Motor - Bipolar
  M2 = Stepper Motor - Bipolar
  MPU9250_MPU-1 = SparkFun IMU Breakout - MPU-9250 [part_number=" SEN-13762"]
  LED1 = LED - 5mm [color="Yellow (595nm)" package="5 mm [THT]"]  # not connected
  LED2 = LED - 5mm [color="Yellow (595nm)" package="5 mm [THT]"]
  LED3 = LED - 5mm [color="Yellow (595nm)" package="5 mm [THT]"]  # not connected
  3_Cell_LiPo = LIPO-2000mAh [part_number="3 Cell LiPo" package=lipo-2000]
  U1 = DC-DC_CONVERTER [package=dc-dc_converter]
  C1 = Electrolytic Capacitor [capacitance=1µF package="100 mil [THT, electrolytic]"]  # not connected
  C2 = Electrolytic Capacitor [capacitance=1µF package="100 mil [THT, electrolytic]"]  # not connected
  R1 = Resistor [tolerance=±20% resistance=220 package=THT]
  R2 = Resistor [tolerance=±20% resistance=220 package=THT]
  R3 = Resistor [tolerance=±20% resistance=220 package=THT]

nets:
  N1: Main_Arduino.A4/SDA, MPU9250_MPU-1.SDA/SDI
  N2: Main_Arduino.A5/SCL, MPU9250_MPU-1.SCL/SCLK
  N3: Main_Arduino.D9_PWM, R1.Pin_1
  N4: Main_Arduino.D10_PWM/SS, Motor_Controller_Arduino.D10
  N5: Main_Arduino.D11_PWM/MOSI, Motor_Controller_Arduino.D11/MOSI
  N6: Main_Arduino.D12/MISO, Motor_Controller_Arduino.D12/MISO
  N7: Main_Arduino.D13/SCK, Motor_Controller_Arduino.D13/SCK
  GND: Main_Arduino.GND, Motor_Controller_Arduino.GND, MPU9250_MPU-1.GND, LED2.cathode, U1.GND2
  N8: Main_Arduino.D5_PWM, R3.Pin_1
  N9: Main_Arduino.D6_PWM, R2.Pin_1
  5V: Main_Arduino.5V, MPU9250_MPU-1.VDD
  VIN: Main_Arduino.VIN, Motor_Controller_Arduino.VIN, U1.VOUT
  N10: Motor_Controller_Arduino.D2, Pololu_A2.DIR
  N11: Motor_Controller_Arduino.D3, Pololu_A2.STEP
  N12: Motor_Controller_Arduino.D4, Pololu_A1.DIR
  N13: Motor_Controller_Arduino.D5, Pololu_A1.STEP
  N14: Motor_Controller_Arduino.D7, Pololu_A2.MS1
  N15: Motor_Controller_Arduino.D8, Pololu_A1.MS1
  VDD: Motor_Controller_Arduino.5V, Pololu_A1.VDD, Pololu_A2.VDD
  N16: Pololu_A1.1B, M1.D
  N17: Pololu_A1.1A, M1.B
  N18: Pololu_A1.2A, M1.C
  N19: Pololu_A1.2B, M1.A
  N20: Pololu_A1.GND#14, 3_Cell_LiPo.-, U1.GND1
  N21: Pololu_A1.VMOT, Pololu_A2.VMOT, 3_Cell_LiPo.+, U1.VIN
  N22: Pololu_A2.1B, M2.D
  N23: Pololu_A2.1A, M2.B
  N24: Pololu_A2.2A, M2.C
  N25: Pololu_A2.2B, M2.A
